# Fritzing sketch Untitled Sketch (saved by Fritzing 0.9.9b)
breadboards: 1

parts:
  LED1 = LED - 5mm [color="Yellow (595nm)" current=0.030 package="5 mm [THT]"]
  Arduino = Arduino Uno (Rev3) - ICSP
  R1 = Resistor [tolerance=±5% power=0.25 resistance=220 package=THT]

nets:
  N1: LED1.cathode, Arduino.GND
  N2: LED1.anode, R1.Pin_0
  N3: Arduino.D2, R1.Pin_1
